# Fritzing sketch RevolvingBlueLight 2 (saved by Fritzing 0.9.3b)
perfboards: 1

parts:
  R1 = Resistor [tolerance=±5% resistance=1.1k package=THT]
  LED1 = LEDs [package=led10mm]
  Q2 = NPN-Transistor [part_number=BC547B package="TO92 [THT]"]
  M1 = DC Motor  # not connected
  Temperature_sensor = Adafruit BME280 [part_number=BME280]
  Wemos_D1_R1 = WeMos D1 R2
  R2 = Resistor [tolerance=±5% resistance=390 package=THT]
  R3 = Resistor [tolerance=±1% resistance=46 package=THT]
  J3 = female pin header, 2 pins [form="♀ (female)"]
  J2 = female pin header, 4 pins [form="♀ (female)"]
  D1 = Diode [part_number=1N4007 package=diode-1n4001]
  J1 = female pin header, 2 pins [form="♀ (female)"]
  Q1 = NPN-Transistor [part_number=BC547B package="TO92 [THT]"]

nets:
  N1: R1.Pin_0, Q1.B
  N2: R1.Pin_1, Wemos_D1_R1.D2, J3.pin1
  N3: LED1.C, Q1.C
  N4: Q2.E, Q1.E
  N5: Q2.B, R2.Pin_0
  N6: Q2.C, J2.pin3, D1.A
  VIN: Temperature_sensor.VIN, Wemos_D1_R1.3.3V
  N7: Temperature_sensor.SCK/SCL, Wemos_D1_R1.D3
  N8: Temperature_sensor.SDI/SDA, Wemos_D1_R1.D4
  N9: Wemos_D1_R1.D1/TX, R2.Pin_1, J3.pin2
  N10: Wemos_D1_R1.GND_3, J1.pin1
  N11: R3.Pin_0, J2.pin2
  N12: R3.Pin_1, D1.C, J1.pin2

custom parts:
  Adafruit BME280: Bosch has stepped up their game with their new BME280 sensor, an environmental sensor with temperature, barometric pressure and humidity! This sensor is great for all sorts of weather/environmental sensing and can even be used in both I2C and SPI! This precision sensor from Bosch is the best low-cost sensing solution for measuring humidity with ±3% accuracy, barometric pressure with ±1 hPa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
  WeMos D1 R2: The D1 R2 is a mini wifi board based on the ESP-8266EX.
