# Fritzing sketch RevolvingBlueLight (saved by Fritzing 0.9.3b)
perfboards: 1

parts:
  R1 = Resistor [tolerance=±5% resistance=1.1k package=THT]
  R2 = Resistor [tolerance=±5% resistance=390 package=THT]
  LED1 = LEDs [package=led10mm]
  D1 = Diode [part_number=1N4007 package=diode-1n4001]
  Q1 = NPN-Transistor [part_number=BC547B package="TO92 [THT]"]
  R3 = Resistor [tolerance=±5% resistance=46 package=THT]
  Q2 = NPN-Transistor [part_number=BC547B package="TO92 [THT]"]
  M1 = DC Motor
  Temperature_sensor = Adafruit BME280 [part_number=BME280]
  Wemos_D1_R1 = WeMos D1 R2

nets:
  N1: R1.Pin_0, Q1.B
  N2: R1.Pin_1, Wemos_D1_R1.D2
  N3: R2.Pin_0, Q2.B
  N4: R2.Pin_1, Wemos_D1_R1.D1/TX
  N5: LED1.C, Q1.C
  N6: LED1.A, R3.Pin_1
  N7: D1.A, Q2.C, M1.pin_2
  N8: D1.C, R3.Pin_0, M1.pin_1, Wemos_D1_R1.5V
  N9: Q1.E, Q2.E
  VIN: Temperature_sensor.VIN, Wemos_D1_R1.3.3V
  N10: Temperature_sensor.SCK/SCL, Wemos_D1_R1.D3
  N11: Temperature_sensor.SDI/SDA, Wemos_D1_R1.D4

custom parts:
  Adafruit BME280: Bosch has stepped up their game with their new BME280 sensor, an environmental sensor with temperature, barometric pressure and humidity! This sensor is great for all sorts of weather/environmental sensing and can even be used in both I2C and SPI! This precision sensor from Bosch is the best low-cost sensing solution for measuring humidity with ±3% accuracy, barometric pressure with ±1 hPa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
  WeMos D1 R2: The D1 R2 is a mini wifi board based on the ESP-8266EX.
